# Fritzing sketch example_1_schema_v1 (saved by Fritzing 0.9.3b)
breadboards: 1

parts:
  R1 = Resistor [tolerance=±5% resistance=1k package=THT]
  N_O = SWITCH-MOMENTARY-2 [package=tactile_switch_smd-2]

nets:
  3.3V: R1.Pin_0
  GPIO 0: R1.Pin_1, N_O.2
  GND: N_O.1
